# Fritzing sketch Wiring Diagram (saved by Fritzing 0.6.3b)
breadboards: 1

parts:
  LED = LED - 5mm [color="Red (633nm)" package="5 mm [THT]"]
  Arduino1 = Arduino
  R1 = Resistor [tolerance=±5% resistance=220 package=THT]
  S1 = Pushbutton [package="[THT]"]
  R2 = Resistor [tolerance=±5% resistance=220 package=THT]

nets:
  N1: LED.cathode, R1.Pin_1
  N2: LED.anode, Arduino1.GND, R2.Pin_0
  N3: Arduino1.D13, R1.Pin_0
  N4: Arduino1.D2, S1.Pin_3, S1.Pin_4, R2.Pin_1
  N5: Arduino1.+5V, S1.Pin_1, S1.Pin_2
